// Logisim project ALU.circ as structural Verilog: 1 circuit, main circuit ALU
module ALU (
  input  [31:0] A,
  input  [31:0] B,
  input  [4:0] Shift,
  input  CarryIn,
  output [3:0] Codop,
  output [31:0] S,
  output [3:0] Flags
);

  wire adder_2_cout, V1, V2, V3;
  wire [31:0] adder_1_out, adder_2_out, adder_3_out, and_1_out, and_2_out, multiplier_1_out, not_1_out,
       not_2_out, or_1_out, or_2_out, shifter_1_out, shifter_2_out, shifter_3_out, shifter_4_out,
       subtractor_1_out, subtractor_2_out, subtractor_3_out, xor_1_out;
  wire [31:1] V4;

  assign and_1_out = A & B;  // AND_Gate and_1, 32 bits wide
  assign xor_1_out = A ^ B;  // XOR_Gate xor_1, 32 bits wide
  Shifter #(.width(32)) shifter_1 (.in(B), .\dist (Shift), .out(shifter_1_out));
  Shifter #(.shift("lr"), .width(32)) shifter_2 (.in(B), .\dist (Shift), .out(shifter_2_out));
  Shifter #(.shift("ar"), .width(32)) shifter_3 (.in(B), .\dist (Shift), .out(shifter_3_out));
  Adder #(.width(32)) adder_1 (.a(A), .b(B), .out(adder_1_out), .cin(CarryIn), .cout(V1));
  Adder #(.width(32)) adder_2 (.a(A), .b(B), .out(adder_2_out), .cin(CarryIn), .cout(adder_2_cout));
  Shifter #(.shift("rr"), .width(32)) shifter_4 (.in(B), .\dist (Shift), .out(shifter_4_out));
  assign and_2_out = A & B;  // AND_Gate and_2, 32 bits wide
  Subtractor #(.width(32)) subtractor_1 (.a({32{1'b0}}), .b(A), .out(subtractor_1_out));  // open: bin, bout
  Subtractor #(.width(32)) subtractor_2 (.a(A), .b(B), .out(subtractor_2_out));  // open: bin, bout
  Adder #(.width(32)) adder_3 (.a(A), .b(B), .out(adder_3_out), .cout(V3));  // open: cin
  Multiplier #(.width(32)) multiplier_1 (.a(A), .b(B), .out(multiplier_1_out), .cout({V4, Flags[3]}));  // open: cin
  assign not_1_out = ~B;  // NOT_Gate not_1, 32 bits wide
  assign not_2_out = ~B;  // NOT_Gate not_2, 32 bits wide
  assign or_1_out = A | B;  // OR_Gate or_1, 32 bits wide
  assign or_2_out = A | not_1_out;  // OR_Gate or_2, 32 bits wide
  Subtractor #(.width(32)) subtractor_3 (
    .a(adder_2_out), .b({32{1'b1}}), .out(subtractor_3_out), .bin(adder_2_cout), .bout(V2));
  Multiplexer #(.enable("false"), .select(4), .width(32)) multiplexer_1 (
    .in0(and_1_out), .in1(xor_1_out), .in2(shifter_1_out), .in3(shifter_2_out), .in4(shifter_3_out),
    .in5(adder_1_out), .in6(subtractor_3_out), .in7(shifter_4_out), .in8(and_2_out), .in9(subtractor_1_out),
    .in10(subtractor_2_out), .in11(adder_3_out), .in12(or_1_out), .in13(multiplier_1_out), .in14(or_2_out),
    .in15(not_2_out), .out(S), .sel(Codop));
  Comparator #(.width(32)) comparator_1 (.a(S), .b({32{1'b0}}), .eq(Flags[1]), .lt(Flags[0]));  // open: gt
  // Pins of 1 and 32 bits meet at {V4, Flags[3]}

  // Other names for the same wires on the sheet: Cin = CarryIn; N = Flags[0]; Z = Flags[1]; C = Flags[2];
  //   V = Flags[3]; V4[0] = Flags[3]

  // Notes on the sheet:
  //   Note: for ROR, C = N
  //   Note 2: assume that shift > 0 for LSL and LSR
  //   Constante = 0
  //   Constante = 1
  //   Constante = 0
endmodule
